// Logisim project Implementation of 4-bit ALU.circ as structural Verilog: 2 circuits, main circuit main
module main (
  input  S0,
  input  S1,
  input  S2,
  input  Ai,
  input  Bi,
  output Xi,
  output Yi
);

  wire and_1_out, and_2_out, and_3_out, and_4_out, and_5_out, and_6_out, and_7_out, and_8_out, not_1_out,
       not_2_out, not_3_out, not_4_out, not_5_out;

  not not_1 (not_1_out, S0);
  not not_2 (not_2_out, S1);
  not not_3 (not_3_out, S2);
  not not_4 (not_4_out, Ai);
  not not_5 (not_5_out, Bi);
  and and_1 (and_1_out, not_1_out, not_2_out, Ai);
  and and_2 (and_2_out, not_1_out, S1, S2);
  and and_3 (and_3_out, S0, not_2_out, S2, Bi);
  and and_4 (and_4_out, S0, S1, not_3_out, Ai);
  and and_5 (and_5_out, not_2_out, S2, Ai);
  and and_6 (and_6_out, not_1_out, not_2_out, S2);
  and and_7 (and_7_out, not_1_out, S2, Ai);
  and and_8 (and_8_out, S1, not_3_out, Ai);
  or or_1 (Yi, and_6_out, and_7_out, and_8_out);
  or or_2 (Xi, and_1_out, and_2_out, and_3_out, and_4_out, and_5_out);
endmodule

module ALU__2 (
  input  S2,
  input  S1,
  input  S0,
  input  A0,
  input  B0,
  input  A1,
  input  B1,
  input  A2,
  input  B2,
  input  A3,
  input  B3,
  output out_12,
  output out_13,
  output out_14,
  output out_15
);

  wire adder_1_cout, adder_2_cout, adder_3_cout, main_1_xi, main_1_yi, main_2_xi, main_2_yi, main_3_xi,
       main_3_yi, main_4_xi, main_4_yi;

  main main_1 (.S0(S2), .S1(S1), .S2(S0), .Ai(A0), .Bi(B0), .Xi(main_1_xi), .Yi(main_1_yi));
  main main_2 (.S0(S2), .S1(S1), .S2(S0), .Ai(A1), .Bi(B1), .Xi(main_2_xi), .Yi(main_2_yi));
  main main_3 (.S0(S2), .S1(S1), .S2(S0), .Ai(A2), .Bi(B2), .Xi(main_3_xi), .Yi(main_3_yi));
  main main_4 (.S0(S2), .S1(S1), .S2(S0), .Ai(A3), .Bi(B3), .Xi(main_4_xi), .Yi(main_4_yi));
  Adder #(.width(1)) adder_1 (.a(main_1_xi), .b(main_1_yi), .out(out_12), .cin(1'b0), .cout(adder_1_cout));
  Adder #(.width(1)) adder_2 (.a(main_2_xi), .b(main_2_yi), .out(out_13), .cin(adder_1_cout), .cout(adder_2_cout));
  Adder #(.width(1)) adder_3 (.a(main_3_xi), .b(main_3_yi), .out(out_14), .cin(adder_2_cout), .cout(adder_3_cout));
  Adder #(.width(1)) adder_4 (.a(main_4_xi), .b(main_4_yi), .out(out_15), .cin(adder_3_cout));  // open: cout
endmodule
